// Digital circuit ALU.dig as structural Verilog
module ALU (
  input  [3:0] in_1,
  input  [7:0] in_2,
  input  [7:0] in_3,
  input  [7:0] in_4,
  input  [7:0] in_5,
  input  [7:0] in_6,
  input  [7:0] in_7
);

  wire and_1_out, and_2_out, not_1_out, opcodes_1_dif, opcodes_1_out_0, opcodes_1_out_1,
       subtrator8bit_1_negativo_out;
  wire [3:0] mut_plicador_1_p_3, mut_plicador_1_p_7, samador8bits_1_c_0, samador8bits_1_c_1,
       subtrator8bit_1_out_0, subtrator8bit_1_out_1;

  opcodes opcodes_1 (.E(in_1), .Out_1(opcodes_1_out_1), .Out_0(opcodes_1_out_0), .Dif(opcodes_1_dif));
  not not_1 (not_1_out, opcodes_1_dif);
  and and_1 (and_1_out, opcodes_1_dif, opcodes_1_out_0);
  and and_2 (and_2_out, opcodes_1_out_0, not_1_out);
  LED led_1 (.in(opcodes_1_out_1));
  LED led_2 (.in(and_2_out));
  LED led_3 (.in(and_1_out));
  mut_plicador mut_plicador_1 (
    .B(in_2), .A(in_3), .P_0(mut_plicador_1_p_3[0]), .P_1(mut_plicador_1_p_3[1]),
    .P_2(mut_plicador_1_p_3[2]), .P_3(mut_plicador_1_p_3[3]), .P_4(mut_plicador_1_p_7[0]),
    .P_5(mut_plicador_1_p_7[1]), .P_6(mut_plicador_1_p_7[2]), .P_7(mut_plicador_1_p_7[3]));  // open: P_8, P_9, P_10, P_11, P_12, P_13, P_14, P_15
  Samador8bits samador8bits_1 (.E_0(in_4), .E_1(in_5), .C_0(samador8bits_1_c_0), .C_1(samador8bits_1_c_1));
  subtrator8bit subtrator8bit_1 (
    .A(in_6), .B(in_7), .Negativo_out(subtrator8bit_1_negativo_out), .Out_0(subtrator8bit_1_out_0),
    .Out_1(subtrator8bit_1_out_1));
  LED led_4 (.in(subtrator8bit_1_negativo_out));
  Seven_Seg_Hex seven_seg_hex_1 (.d(samador8bits_1_c_0), .dp(1'b0));
  Seven_Seg_Hex seven_seg_hex_2 (.d(subtrator8bit_1_out_0), .dp(1'b0));
  Seven_Seg_Hex seven_seg_hex_3 (.d(samador8bits_1_c_1), .dp(1'b0));
  Seven_Seg_Hex seven_seg_hex_4 (.d(subtrator8bit_1_out_1), .dp(1'b0));
  Seven_Seg_Hex seven_seg_hex_5 (.d(mut_plicador_1_p_3), .dp(1'b0));
  Seven_Seg_Hex seven_seg_hex_6 (.d(mut_plicador_1_p_7), .dp(1'b0));
endmodule
