// Digital circuit HalfAdder.dig as structural Verilog
module HalfAdder (
  input  A_0,
  input  A_1,
  input  A_2,
  input  A_3,
  input  A_4,
  input  A_5,
  input  A_6,
  input  A_7,
  input  B_0,
  input  B_1,
  input  B_2,
  input  B_3,
  input  B_4,
  input  B_5,
  input  B_6,
  input  B_7,
  output S_0,
  output S_1,
  output S_2,
  output S_3,
  output S_4,
  output S_5,
  output S_6,
  output S_7,
  output C_out
);

  wire somador_1_c_out, somador_2_c_out, somador_3_c_out, somador_4_c_out, somador_5_c_out, somador_6_c_out,
       somador_7_c_out;

  somador somador_1 (.A(A_0), .B(B_0), .C_in(1'b0), .S(S_0), .C_out(somador_1_c_out));
  somador somador_2 (.A(A_1), .B(B_1), .C_in(somador_1_c_out), .S(S_1), .C_out(somador_2_c_out));
  somador somador_3 (.A(A_2), .B(B_2), .C_in(somador_2_c_out), .S(S_2), .C_out(somador_3_c_out));
  somador somador_4 (.A(A_3), .B(B_3), .C_in(somador_3_c_out), .S(S_3), .C_out(somador_4_c_out));
  somador somador_5 (.A(A_4), .B(B_4), .C_in(somador_4_c_out), .S(S_4), .C_out(somador_5_c_out));
  somador somador_6 (.A(A_5), .B(B_5), .C_in(somador_5_c_out), .S(S_5), .C_out(somador_6_c_out));
  somador somador_7 (.A(A_6), .B(B_6), .C_in(somador_6_c_out), .S(S_6), .C_out(somador_7_c_out));
  somador somador_8 (.A(A_7), .B(B_7), .C_in(somador_7_c_out), .S(S_7), .C_out(C_out));
endmodule
