// Digital circuit Samador8bits.dig as structural Verilog
module Samador8bits (
  input  [7:0] E_0,
  input  [7:0] E_1,
  output [7:0] C_0,
  output [7:0] C_1
);

  wire somador_1_c_out, somador_2_c_out, somador_3_c_out, somador_4_c_out, somador_5_c_out, somador_6_c_out,
       somador_7_c_out, somador_8_c_out;

  somador somador_1 (.A(E_0[0]), .B(E_1[0]), .C_in(1'b0), .S(C_0[0]), .C_out(somador_1_c_out));
  somador somador_2 (.A(E_0[1]), .B(E_1[1]), .C_in(somador_1_c_out), .S(C_0[1]), .C_out(somador_2_c_out));
  somador somador_3 (.A(E_0[2]), .B(E_1[2]), .C_in(somador_2_c_out), .S(C_0[2]), .C_out(somador_3_c_out));
  somador somador_4 (.A(E_0[3]), .B(E_1[3]), .C_in(somador_3_c_out), .S(C_0[3]), .C_out(somador_4_c_out));
  somador somador_5 (.A(E_0[4]), .B(E_1[4]), .C_in(somador_4_c_out), .S(C_1[0]), .C_out(somador_5_c_out));
  somador somador_6 (.A(E_0[5]), .B(E_1[5]), .C_in(somador_5_c_out), .S(C_1[1]), .C_out(somador_6_c_out));
  somador somador_7 (.A(E_0[6]), .B(E_1[6]), .C_in(somador_6_c_out), .S(C_1[2]), .C_out(somador_7_c_out));
  somador somador_8 (.A(E_0[7]), .B(E_1[7]), .C_in(somador_7_c_out), .S(C_1[3]), .C_out(somador_8_c_out));
  // Pins of 4 and 8 bits meet at C_0
  // Pins of 4 and 8 bits meet at C_1
  // also tied to GND on the sheet: somador_8_c_out
endmodule
