// Digital circuit mut´plicador.dig as structural Verilog
module mut_plicador (
  input  [7:0] B,
  input  [7:0] A,
  output P_0,
  output P_1,
  output P_2,
  output P_3,
  output P_4,
  output P_5,
  output P_6,
  output P_7,
  output P_8,
  output P_9,
  output P_10,
  output P_11,
  output P_12,
  output P_13,
  output P_14,
  output P_15
);

  wire and_1_out, and_2_out, and_3_out, and_4_out, and_5_out, and_6_out, and_7_out, and_8_out, and_9_out,
       and_10_out, and_11_out, and_12_out, and_13_out, and_14_out, and_15_out, and_16_out, and_17_out,
       and_18_out, and_19_out, and_20_out, and_21_out, and_22_out, and_23_out, and_24_out, and_25_out,
       and_26_out, and_27_out, and_28_out, and_29_out, and_30_out, and_31_out, and_32_out, and_33_out,
       and_34_out, and_35_out, and_36_out, and_37_out, and_38_out, and_39_out, and_40_out, and_41_out,
       and_42_out, and_43_out, and_44_out, and_45_out, and_46_out, and_47_out, and_48_out, and_49_out,
       and_50_out, and_51_out, and_52_out, and_53_out, and_54_out, and_55_out, and_56_out, and_57_out,
       and_58_out, and_59_out, and_60_out, and_61_out, and_62_out, and_63_out, halfadder_2_c_out,
       halfadder_2_s_1, halfadder_2_s_2, halfadder_2_s_3, halfadder_2_s_4, halfadder_2_s_5, halfadder_2_s_6,
       halfadder_2_s_7, halfadder_3_c_out, halfadder_3_s_1, halfadder_3_s_2, halfadder_3_s_3,
       halfadder_3_s_4, halfadder_3_s_5, halfadder_3_s_6, halfadder_3_s_7, halfadder_4_c_out,
       halfadder_4_s_1, halfadder_4_s_2, halfadder_4_s_3, halfadder_4_s_4, halfadder_4_s_5, halfadder_4_s_6,
       halfadder_4_s_7, halfadder_5_c_out, halfadder_5_s_1, halfadder_5_s_2, halfadder_5_s_3,
       halfadder_5_s_4, halfadder_5_s_5, halfadder_5_s_6, halfadder_5_s_7, halfadder_6_c_out,
       halfadder_6_s_1, halfadder_6_s_2, halfadder_6_s_3, halfadder_6_s_4, halfadder_6_s_5, halfadder_6_s_6,
       halfadder_6_s_7, halfadder_7_c_out, halfadder_7_s_1, halfadder_7_s_2, halfadder_7_s_3,
       halfadder_7_s_4, halfadder_7_s_5, halfadder_7_s_6, halfadder_7_s_7;

  and and_1 (and_1_out, A[7], B[5]);
  and and_2 (and_2_out, A[7], B[7]);
  and and_3 (and_3_out, A[6], B[5]);
  and and_4 (and_4_out, A[5], B[5]);
  and and_5 (and_5_out, A[6], B[7]);
  and and_6 (and_6_out, A[5], B[7]);
  and and_7 (and_7_out, A[4], B[5]);
  and and_8 (and_8_out, A[3], B[5]);
  and and_9 (and_9_out, A[4], B[7]);
  and and_10 (and_10_out, A[3], B[7]);
  and and_11 (and_11_out, A[2], B[5]);
  and and_12 (and_12_out, A[1], B[5]);
  and and_13 (and_13_out, A[2], B[7]);
  and and_14 (and_14_out, A[1], B[7]);
  and and_15 (and_15_out, A[0], B[5]);
  and and_16 (and_16_out, A[0], B[7]);
  and and_17 (and_17_out, A[7], B[6]);
  and and_18 (and_18_out, A[6], B[6]);
  and and_19 (and_19_out, A[7], B[3]);
  and and_20 (and_20_out, A[5], B[6]);
  and and_21 (and_21_out, A[7], B[2]);
  and and_22 (and_22_out, A[4], B[6]);
  and and_23 (and_23_out, A[6], B[3]);
  and and_24 (and_24_out, A[7], B[4]);
  and and_25 (and_25_out, A[6], B[2]);
  and and_26 (and_26_out, A[5], B[3]);
  and and_27 (and_27_out, A[3], B[6]);
  and and_28 (and_28_out, A[5], B[2]);
  and and_29 (and_29_out, A[6], B[4]);
  and and_30 (and_30_out, A[2], B[6]);
  and and_31 (and_31_out, A[4], B[3]);
  and and_32 (and_32_out, A[5], B[4]);
  and and_33 (and_33_out, A[4], B[2]);
  and and_34 (and_34_out, A[3], B[3]);
  and and_35 (and_35_out, A[1], B[6]);
  and and_36 (and_36_out, A[3], B[2]);
  and and_37 (and_37_out, A[4], B[4]);
  and and_38 (and_38_out, A[0], B[6]);
  and and_39 (and_39_out, A[2], B[3]);
  and and_40 (and_40_out, A[3], B[4]);
  and and_41 (and_41_out, A[2], B[2]);
  and and_42 (and_42_out, A[1], B[3]);
  and and_43 (and_43_out, A[1], B[2]);
  and and_44 (and_44_out, A[2], B[4]);
  HalfAdder halfadder_1 (
    .A_0(halfadder_2_s_1), .A_1(halfadder_2_s_2), .A_2(halfadder_2_s_3), .A_3(halfadder_2_s_4),
    .A_4(halfadder_2_s_5), .A_5(halfadder_2_s_6), .A_6(halfadder_2_s_7), .A_7(halfadder_2_c_out),
    .B_0(and_16_out), .B_1(and_14_out), .B_2(and_13_out), .B_3(and_10_out), .B_4(and_9_out), .B_5(and_6_out),
    .B_6(and_5_out), .B_7(and_2_out), .S_0(P_7), .S_1(P_8), .S_2(P_9), .S_3(P_10), .S_4(P_11), .S_5(P_12),
    .S_6(P_13), .S_7(P_14), .C_out(P_15));
  and and_45 (and_45_out, A[0], B[3]);
  and and_46 (and_46_out, A[1], B[4]);
  and and_47 (and_47_out, A[0], B[2]);
  and and_48 (and_48_out, A[0], B[4]);
  HalfAdder halfadder_2 (
    .A_0(halfadder_3_s_1), .A_1(halfadder_3_s_2), .A_2(halfadder_3_s_3), .A_3(halfadder_3_s_4),
    .A_4(halfadder_3_s_5), .A_5(halfadder_3_s_6), .A_6(halfadder_3_s_7), .A_7(halfadder_3_c_out),
    .B_0(and_38_out), .B_1(and_35_out), .B_2(and_30_out), .B_3(and_27_out), .B_4(and_22_out),
    .B_5(and_20_out), .B_6(and_18_out), .B_7(and_17_out), .S_0(P_6), .S_1(halfadder_2_s_1),
    .S_2(halfadder_2_s_2), .S_3(halfadder_2_s_3), .S_4(halfadder_2_s_4), .S_5(halfadder_2_s_5),
    .S_6(halfadder_2_s_6), .S_7(halfadder_2_s_7), .C_out(halfadder_2_c_out));
  and and_49 (and_49_out, A[7], B[1]);
  and and_50 (and_50_out, A[7], B[0]);
  HalfAdder halfadder_3 (
    .A_0(halfadder_4_s_3), .A_1(halfadder_4_s_2), .A_2(halfadder_4_s_1), .A_3(halfadder_4_s_4),
    .A_4(halfadder_4_s_5), .A_5(halfadder_4_s_6), .A_6(halfadder_4_s_7), .A_7(halfadder_4_c_out),
    .B_0(and_15_out), .B_1(and_12_out), .B_2(and_11_out), .B_3(and_8_out), .B_4(and_7_out), .B_5(and_4_out),
    .B_6(and_3_out), .B_7(and_1_out), .S_0(P_5), .S_1(halfadder_3_s_1), .S_2(halfadder_3_s_2),
    .S_3(halfadder_3_s_3), .S_4(halfadder_3_s_4), .S_5(halfadder_3_s_5), .S_6(halfadder_3_s_6),
    .S_7(halfadder_3_s_7), .C_out(halfadder_3_c_out));
  and and_51 (and_51_out, A[6], B[1]);
  and and_52 (and_52_out, A[6], B[0]);
  and and_53 (and_53_out, A[5], B[1]);
  and and_54 (and_54_out, A[5], B[0]);
  HalfAdder halfadder_4 (
    .A_0(halfadder_6_s_4), .A_1(halfadder_6_s_1), .A_2(halfadder_6_s_2), .A_3(halfadder_6_s_3),
    .A_4(halfadder_6_s_5), .A_5(halfadder_6_s_6), .A_6(halfadder_6_s_7), .A_7(halfadder_6_c_out),
    .B_0(and_48_out), .B_1(and_46_out), .B_2(and_44_out), .B_3(and_40_out), .B_4(and_37_out),
    .B_5(and_32_out), .B_6(and_29_out), .B_7(and_24_out), .S_0(P_4), .S_1(halfadder_4_s_1),
    .S_2(halfadder_4_s_2), .S_3(halfadder_4_s_3), .S_4(halfadder_4_s_4), .S_5(halfadder_4_s_5),
    .S_6(halfadder_4_s_6), .S_7(halfadder_4_s_7), .C_out(halfadder_4_c_out));
  and and_55 (and_55_out, A[4], B[1]);
  and and_56 (and_56_out, A[4], B[0]);
  and and_57 (and_57_out, A[3], B[1]);
  and and_58 (and_58_out, A[3], B[0]);
  and and_59 (and_59_out, A[2], B[1]);
  and and_60 (and_60_out, A[2], B[0]);
  and and_61 (and_61_out, A[1], B[1]);
  and and_62 (and_62_out, A[1], B[0]);
  HalfAdder halfadder_5 (
    .A_0(halfadder_7_s_1), .A_1(halfadder_7_s_2), .A_2(halfadder_7_s_3), .A_3(halfadder_7_s_4),
    .A_4(halfadder_7_s_5), .A_5(halfadder_7_s_6), .A_6(halfadder_7_s_7), .A_7(halfadder_7_c_out),
    .B_0(and_47_out), .B_1(and_43_out), .B_2(and_41_out), .B_3(and_36_out), .B_4(and_33_out),
    .B_5(and_28_out), .B_6(and_25_out), .B_7(and_21_out), .S_0(P_2), .S_1(halfadder_5_s_1),
    .S_2(halfadder_5_s_2), .S_3(halfadder_5_s_3), .S_4(halfadder_5_s_4), .S_5(halfadder_5_s_5),
    .S_6(halfadder_5_s_6), .S_7(halfadder_5_s_7), .C_out(halfadder_5_c_out));
  HalfAdder halfadder_6 (
    .A_0(halfadder_5_s_3), .A_1(halfadder_5_s_1), .A_2(halfadder_5_s_2), .A_3(halfadder_5_s_4),
    .A_4(halfadder_5_s_5), .A_5(halfadder_5_s_6), .A_6(halfadder_5_s_7), .A_7(halfadder_5_c_out),
    .B_0(and_45_out), .B_1(and_42_out), .B_2(and_39_out), .B_3(and_34_out), .B_4(and_31_out),
    .B_5(and_26_out), .B_6(and_23_out), .B_7(and_19_out), .S_0(P_3), .S_1(halfadder_6_s_1),
    .S_2(halfadder_6_s_2), .S_3(halfadder_6_s_3), .S_4(halfadder_6_s_4), .S_5(halfadder_6_s_5),
    .S_6(halfadder_6_s_6), .S_7(halfadder_6_s_7), .C_out(halfadder_6_c_out));
  and and_63 (and_63_out, A[0], B[1]);
  HalfAdder halfadder_7 (
    .A_0(and_63_out), .A_1(and_61_out), .A_2(and_62_out), .A_3(and_60_out), .A_4(and_59_out),
    .A_5(and_58_out), .A_6(and_57_out), .A_7(1'b0), .B_0(and_56_out), .B_1(and_55_out), .B_2(and_54_out),
    .B_3(and_53_out), .B_4(and_52_out), .B_5(and_51_out), .B_6(and_50_out), .B_7(and_49_out), .S_0(P_1),
    .S_1(halfadder_7_s_1), .S_2(halfadder_7_s_2), .S_3(halfadder_7_s_3), .S_4(halfadder_7_s_4),
    .S_5(halfadder_7_s_5), .S_6(halfadder_7_s_6), .S_7(halfadder_7_s_7), .C_out(halfadder_7_c_out));
  and and_64 (P_0, A[0], B[0]);
endmodule
