// Digital circuit opcodes.dig as structural Verilog
module opcodes (
  input  [3:0] E,
  output Out_1,
  output Out_0,
  output Dif
);

  wire not_1_out;

  not not_1 (not_1_out, E[0]);
  and and_1 (Out_1, not_1_out, E[1]);
  and and_2 (Dif, E[1], E[0]);

  assign Out_0 = E[0];
endmodule
