// Digital circuit subtrator1bit.dig as structural Verilog
module subtrator1bit (
  input  A,
  input  B,
  input  T_in,
  output S,
  output T_out
);

  wire and_1_out, and_2_out, and_3_out, not_1_out, not_2_out, xor_1_out;

  xor xor_1 (xor_1_out, A, B);
  and and_1 (and_1_out, B, T_in);
  and and_2 (and_2_out, T_in, not_1_out);
  not not_1 (not_1_out, A);
  and and_3 (and_3_out, B, not_2_out);
  not not_2 (not_2_out, A);
  xor xor_2 (S, xor_1_out, T_in);
  or or_1 (T_out, and_1_out, and_2_out, and_3_out);
endmodule
