// Digital circuit subtrator8bit.dig as structural Verilog
module subtrator8bit (
  input  [7:0] A,
  input  [7:0] B,
  output Negativo_out,
  output [3:0] Out_0,
  output [3:0] Out_1
);

  wire subtrator1bit_1_t_out, subtrator1bit_2_t_out, subtrator1bit_3_t_out, subtrator1bit_4_t_out,
       subtrator1bit_5_t_out, subtrator1bit_6_t_out, subtrator1bit_7_t_out;

  subtrator1bit subtrator1bit_1 (.A(A[0]), .B(B[0]), .T_in(1'b0), .S(Out_0[0]), .T_out(subtrator1bit_1_t_out));
  subtrator1bit subtrator1bit_2 (
    .A(A[1]), .B(B[1]), .T_in(subtrator1bit_1_t_out), .S(Out_0[1]), .T_out(subtrator1bit_2_t_out));
  subtrator1bit subtrator1bit_3 (
    .A(A[2]), .B(B[2]), .T_in(subtrator1bit_2_t_out), .S(Out_0[2]), .T_out(subtrator1bit_3_t_out));
  subtrator1bit subtrator1bit_4 (
    .A(A[3]), .B(B[3]), .T_in(subtrator1bit_3_t_out), .S(Out_0[3]), .T_out(subtrator1bit_4_t_out));
  subtrator1bit subtrator1bit_5 (
    .A(A[4]), .B(B[4]), .T_in(subtrator1bit_4_t_out), .S(Out_1[0]), .T_out(subtrator1bit_5_t_out));
  subtrator1bit subtrator1bit_6 (
    .A(A[5]), .B(B[5]), .T_in(subtrator1bit_5_t_out), .S(Out_1[1]), .T_out(subtrator1bit_6_t_out));
  subtrator1bit subtrator1bit_7 (
    .A(A[6]), .B(B[6]), .T_in(subtrator1bit_6_t_out), .S(Out_1[2]), .T_out(subtrator1bit_7_t_out));
  subtrator1bit subtrator1bit_8 (.A(A[7]), .B(B[7]), .T_in(subtrator1bit_7_t_out), .S(Out_1[3]), .T_out(Negativo_out));
endmodule
